// Logisim project Pipelined_Floating_Point_Multiplier.circ as structural Verilog: 1 circuit, main circuit Pipeline
module Pipeline (
);

  wire Clock_out, Sign1_q, xor_1_out;
  wire [7:0] adder_1_out, adder_2_out, Address_Register_q, Exponent_q, subtractor_1_out;
  wire [22:0] A2_q_2, B2_q_2, multiplexer_1_out;
  wire [23:0] multiplier_1_cout, multiplier_1_out;
  wire [31:0] A1_q, B1_q, rom_1_data, rom_2_data;
  wire [31:23] A2_q, B2_q;
  wire [31:31] Sign2_q;

  Counter Address_Register (.Q(Address_Register_q), .clk(Clock_out));  // open: load, D, count, carry, clr
  Clock Clock (.out(Clock_out));
  ROM #(.dataWidth(32)) rom_1 (.addr(Address_Register_q), .data(rom_1_data));  // open: sel
  ROM #(.dataWidth(32)) rom_2 (.addr(Address_Register_q), .data(rom_2_data));  // open: sel
  Register #(.width(1)) Sign1 (.D(xor_1_out), .Q(Sign1_q), .clk(Clock_out));  // open: en, clr
  xor xor_1 (xor_1_out, rom_1_data[31], rom_2_data[31]);
  Register #(.width(32)) B1 (.D(rom_2_data), .Q(B1_q), .clk(Clock_out));  // open: en, clr
  Register #(.width(32)) A1 (.D(rom_1_data), .Q(A1_q), .clk(Clock_out));  // open: en, clr
  Adder adder_1 (.a(A1_q[30:23]), .b(B1_q[30:23]), .out(adder_1_out));  // open: cin, cout
  Register #(.width(1)) Sign2 (.D(Sign1_q), .Q(Sign2_q[31]), .clk(Clock_out));  // open: en, clr
  Subtractor subtractor_1 (.a(adder_1_out), .b(8'h7f), .out(subtractor_1_out));  // open: bin, bout
  Register Exponent (.D(subtractor_1_out), .Q(Exponent_q), .clk(Clock_out));  // open: en, clr
  Register #(.width(32)) B2 (.D(B1_q), .Q({B2_q, B2_q_2}), .clk(Clock_out));  // open: en, clr
  Register #(.width(32)) A2 (.D(A1_q), .Q({A2_q, A2_q_2}), .clk(Clock_out));  // open: en, clr
  Multiplier #(.width(24)) multiplier_1 (
    .a({1'b1, A2_q_2}), .b({1'b1, B2_q_2}), .out(multiplier_1_out), .cout(multiplier_1_cout));  // open: cin
  Multiplexer #(.width(23), .enable("false")) multiplexer_1 (
    .in0({multiplier_1_cout[21:0], multiplier_1_out[23]}), .in1(multiplier_1_cout[22:0]),
    .out(multiplexer_1_out), .sel(multiplier_1_cout[23]));
  Adder adder_2 (.a(Exponent_q), .b({8{1'b0}}), .out(adder_2_out), .cin(multiplier_1_cout[23]));  // open: cout
  RAM #(.dataWidth(32), .bus("separate")) ram_1 (
    .addr(Address_Register_q), .din({Sign2_q[31], adder_2_out, multiplexer_1_out}), .str(1'b1),
    .clk(Clock_out));  // open: data, sel, ld, clr

  // Notes on the sheet:
  //   contents of rom_1 (hex, n*v repeats v):
  //   42fa4000 42fa8000 c6460000 3faf8000
  //   contents of rom_2 (hex, n*v repeats v):
  //   41410000 45450000 c4251000 bf920000
  //   Pipelined Floating Point Multiplier
endmodule
